// Logisim project ula-reg.circ as structural Verilog
module mux2 (
  input  in_1,
  input  in_2,
  input  SelM2,
  output out_4
);

  wire and_1_out, and_2_out;

  and and_1 (and_1_out, in_1, ~SelM2);  // AND_Gate
  and and_2 (and_2_out, in_2, SelM2);
  or or_1 (out_4, and_1_out, and_2_out);
endmodule

module mux8 (
  input  in_1,
  input  in_2,
  input  in_3,
  input  in_4,
  input  in_5,
  input  in_6,
  input  in_7,
  input  in_8,
  input  [2:0] SelM8,
  output out_10
);

  wire and_1_out, and_2_out, and_3_out, and_4_out, and_5_out, and_6_out, and_7_out, and_8_out;

  and and_1 (and_1_out, in_1, ~SelM8[2], ~SelM8[1], ~SelM8[0]);  // AND_Gate
  and and_2 (and_2_out, in_2, ~SelM8[2], ~SelM8[1], SelM8[0]);  // AND_Gate
  and and_3 (and_3_out, in_3, ~SelM8[2], SelM8[1], ~SelM8[0]);  // AND_Gate
  and and_4 (and_4_out, in_4, ~SelM8[2], SelM8[1], SelM8[0]);  // AND_Gate
  and and_5 (and_5_out, in_5, SelM8[2], ~SelM8[1], ~SelM8[0]);  // AND_Gate
  and and_6 (and_6_out, in_6, SelM8[2], SelM8[1], ~SelM8[0]);  // AND_Gate
  and and_7 (and_7_out, in_7, SelM8[2], ~SelM8[1], SelM8[0]);  // AND_Gate
  and and_8 (and_8_out, in_8, SelM8[2], SelM8[1], SelM8[0]);
  or or_1 (out_10, and_1_out, and_2_out, and_3_out, and_4_out, and_5_out, and_6_out, and_7_out, and_8_out);
endmodule

module mux16 (
  input  [7:0] in_1,
  input  [7:0] in_2,
  input  [3:0] selM16,
  output out_4
);

  wire mux8_1_out_10, mux8_2_out_10;

  mux8 mux8_1 (
    .in_1(in_1[0]), .in_2(in_1[1]), .in_3(in_1[2]), .in_4(in_1[3]), .in_5(in_1[4]), .in_6(in_1[5]),
    .in_7(in_1[6]), .in_8(in_1[7]), .out_10(mux8_1_out_10), .SelM8(selM16[2:0]));
  mux8 mux8_2 (
    .in_1(in_2[0]), .in_2(in_2[1]), .in_3(in_2[2]), .in_4(in_2[3]), .in_5(in_2[4]), .in_6(in_2[5]),
    .in_7(in_2[6]), .in_8(in_2[7]), .out_10(mux8_2_out_10), .SelM8(selM16[2:0]));
  mux2 mux2_1 (.in_1(mux8_1_out_10), .in_2(mux8_2_out_10), .out_4(out_4), .SelM2(selM16[3]));
endmodule

module Somador_Completo (
  input  Vem1,
  input  a,
  input  b,
  output Soma,
  output Vai1
);

  wire and_1_out, and_2_out, and_3_out, xor_1_out;

  xor xor_1 (xor_1_out, a, b);
  and and_1 (and_1_out, a, Vem1);
  and and_2 (and_2_out, a, b);
  and and_3 (and_3_out, b, Vem1);
  xor xor_2 (Soma, Vem1, xor_1_out);
  or or_1 (Vai1, and_1_out, and_2_out, and_3_out);
endmodule

module ULAcell (
  input  B,
  input  A,
  input  [3:0] OperCode,
  input  Vem1,
  output \Saída ,
  output Vai1
);

  wire [3:0] and_1_out;
  wire [7:1] nand_1_out;

  Somador_Completo somador_completo_1 (.Vem1(Vem1), .a(A), .b(B), .Soma(and_1_out[3]), .Vai1(Vai1));
  nand nand_1 (nand_1_out[1], B, A);
  and and_1 (and_1_out[0], B, A);
  or or_1 (and_1_out[1], B, A);
  xor xor_1 (and_1_out[2], B, A);
  mux16 mux16_1 (.in_1({{4{B}}, and_1_out}), .in_2({nand_1_out, B}), .out_4(\Saída ), .selM16(OperCode));
endmodule

module sll1bit (
  input  [31:0] Entrada,
  input  Shift,
  output [31:0] \Saída 
);

  Multiplexer #(.width(32), .enable("false")) multiplexer_1 (
    .in0(Entrada), .in1({Entrada[30:0], 1'b0}), .out(\Saída ), .sel(Shift));
endmodule

module sll1bit_detector (
  input  [3:0] OperCOde,
  output \Saída 
);

  and and_1 (\Saída , ~OperCOde[3], OperCOde[2], ~OperCOde[1], OperCOde[0]);  // AND_Gate
endmodule

module srl1bit (
  input  [31:0] Entrada,
  input  Shift,
  output [31:0] \Saída 
);

  Multiplexer #(.width(32), .enable("false")) multiplexer_1 (
    .in0(Entrada), .in1({1'b0, Entrada[31:1]}), .out(\Saída ), .sel(Shift));
endmodule

module srl1bit_detector (
  input  [3:0] OperCOde,
  output \Saída 
);

  and and_1 (\Saída , ~OperCOde[3], OperCOde[2], OperCOde[1], ~OperCOde[0]);  // AND_Gate
endmodule

module sra1bit (
  input  [31:0] Entrada,
  input  Shift,
  output [31:0] \Saída 
);

  Multiplexer #(.width(32), .enable("false")) multiplexer_1 (
    .in0(Entrada), .in1({{2{Entrada[31]}}, Entrada[30:1]}), .out(\Saída ), .sel(Shift));
endmodule

module sra_detector (
  input  [3:0] OperCOde,
  output \Saída 
);

  and and_1 (\Saída , ~OperCOde[3], OperCOde[2], OperCOde[1], OperCOde[0]);  // AND_Gate
endmodule

module lua16bits (
  input  [31:0] Entrada,
  input  Shift,
  output [31:0] Entrada_2
);

  Multiplexer #(.width(32), .enable("false")) multiplexer_1 (
    .in0(Entrada),
    .in1({Entrada[0], Entrada[1], Entrada[2], Entrada[3], Entrada[4], Entrada[5], Entrada[6], Entrada[7], Entrada[8], Entrada[9], Entrada[10], Entrada[11], Entrada[12], Entrada[13], Entrada[14], Entrada[15], {16{1'b0}}}),
    .out(Entrada_2), .sel(Shift));
endmodule

module lua_detector (
  input  [3:0] OperCOde,
  output \Saída 
);

  and and_1 (\Saída , OperCOde[3], ~OperCOde[2], ~OperCOde[1], ~OperCOde[0]);  // AND_Gate
endmodule

module ULA (
  input  [31:0] A,
  input  [31:0] B,
  input  [3:0] OperCode,
  output [31:0] \Saída ,
  output out_5
);

  wire B0, B1, B2, B3, B4, B5, B6, B7, B8, B9, B10, B11, B12, B13, B14, B15, B16, B17, B18, B19, B20, B21,
       B22, B23, B24, B25, B26, B27, B28, B29, B30, B31, \lua_detector_1_saída , \sll1bit_detector_1_saída ,
       \sra_detector_1_saída , \srl1bit_detector_1_saída , ulacell_1_vai1, ulacell_2_vai1, ulacell_3_vai1,
       ulacell_4_vai1, ulacell_5_vai1, ulacell_6_vai1, ulacell_7_vai1, ulacell_8_vai1, ulacell_9_vai1,
       ulacell_10_vai1, ulacell_11_vai1, ulacell_12_vai1, ulacell_13_vai1, ulacell_14_vai1, ulacell_15_vai1,
       ulacell_16_vai1, ulacell_17_vai1, ulacell_18_vai1, ulacell_19_vai1, ulacell_20_vai1, ulacell_21_vai1,
       ulacell_22_vai1, ulacell_23_vai1, ulacell_24_vai1, ulacell_25_vai1, ulacell_26_vai1, ulacell_27_vai1,
       ulacell_28_vai1, ulacell_29_vai1, ulacell_30_vai1, ulacell_31_vai1;
  wire [31:0] \sll1bit_1_saída , \sra1bit_1_saída , \srl1bit_1_saída ;

  ULAcell ulacell_1 (
    .Vai1(ulacell_1_vai1), .\Saída (\Saída [15]), .Vem1(ulacell_3_vai1), .B(A[15]), .A(A[15]),
    .OperCode(OperCode));
  ULAcell ulacell_2 (
    .Vai1(ulacell_2_vai1), .\Saída (\Saída [16]), .Vem1(ulacell_1_vai1), .B(B16), .A(A[16]),
    .OperCode(OperCode));
  ULAcell ulacell_3 (
    .Vai1(ulacell_3_vai1), .\Saída (\Saída [14]), .Vem1(ulacell_5_vai1), .B(B14), .A(A[14]),
    .OperCode(OperCode));
  ULAcell ulacell_4 (
    .Vai1(ulacell_4_vai1), .\Saída (\Saída [17]), .Vem1(ulacell_2_vai1), .B(B17), .A(A[17]),
    .OperCode(OperCode));
  ULAcell ulacell_5 (
    .Vai1(ulacell_5_vai1), .\Saída (\Saída [13]), .Vem1(ulacell_7_vai1), .B(B13), .A(A[13]),
    .OperCode(OperCode));
  ULAcell ulacell_6 (
    .Vai1(ulacell_6_vai1), .\Saída (\Saída [18]), .Vem1(ulacell_4_vai1), .B(B18), .A(A[18]),
    .OperCode(OperCode));
  ULAcell ulacell_7 (
    .Vai1(ulacell_7_vai1), .\Saída (\Saída [12]), .Vem1(ulacell_9_vai1), .B(B12), .A(A[12]),
    .OperCode(OperCode));
  ULAcell ulacell_8 (
    .Vai1(ulacell_8_vai1), .\Saída (\Saída [19]), .Vem1(ulacell_6_vai1), .B(B19), .A(A[19]),
    .OperCode(OperCode));
  ULAcell ulacell_9 (
    .Vai1(ulacell_9_vai1), .\Saída (\Saída [11]), .Vem1(ulacell_11_vai1), .B(B11), .A(A[11]),
    .OperCode(OperCode));
  ULAcell ulacell_10 (
    .Vai1(ulacell_10_vai1), .\Saída (\Saída [20]), .Vem1(ulacell_8_vai1), .B(B20), .A(A[20]),
    .OperCode(OperCode));
  lua16bits lua16bits_1 (
    .Entrada(\sra1bit_1_saída ),
    .Entrada_2({B31, B30, B29, B28, B27, B26, B25, B24, B23, B22, B21, B20, B19, B18, B17, B16, B15, B14, B13, B12, B11, B10, B9, B8, B7, B6, B5, B4, B3, B2, B1, B0}),
    .Shift(\lua_detector_1_saída ));
  lua_detector lua_detector_1 (.\Saída (\lua_detector_1_saída ), .OperCOde(OperCode));
  ULAcell ulacell_11 (
    .Vai1(ulacell_11_vai1), .\Saída (\Saída [10]), .Vem1(ulacell_13_vai1), .B(B10), .A(A[10]),
    .OperCode(OperCode));
  ULAcell ulacell_12 (
    .Vai1(ulacell_12_vai1), .\Saída (\Saída [21]), .Vem1(ulacell_10_vai1), .B(B21), .A(A[21]),
    .OperCode(OperCode));
  sra1bit sra1bit_1 (.Entrada(\srl1bit_1_saída ), .\Saída (\sra1bit_1_saída ), .Shift(\sra_detector_1_saída ));
  sra_detector sra_detector_1 (.\Saída (\sra_detector_1_saída ), .OperCOde(OperCode));
  ULAcell ulacell_13 (
    .Vai1(ulacell_13_vai1), .\Saída (\Saída [9]), .Vem1(ulacell_15_vai1), .B(B9), .A(A[9]),
    .OperCode(OperCode));
  ULAcell ulacell_14 (
    .Vai1(ulacell_14_vai1), .\Saída (\Saída [22]), .Vem1(ulacell_12_vai1), .B(B22), .A(A[22]),
    .OperCode(OperCode));
  srl1bit srl1bit_1 (.Entrada(\sll1bit_1_saída ), .\Saída (\srl1bit_1_saída ), .Shift(\srl1bit_detector_1_saída ));
  sll1bit sll1bit_1 (.Entrada(B), .\Saída (\sll1bit_1_saída ), .Shift(\sll1bit_detector_1_saída ));
  srl1bit_detector srl1bit_detector_1 (.\Saída (\srl1bit_detector_1_saída ), .OperCOde(OperCode));
  sll1bit_detector sll1bit_detector_1 (.\Saída (\sll1bit_detector_1_saída ), .OperCOde(OperCode));
  ULAcell ulacell_15 (
    .Vai1(ulacell_15_vai1), .\Saída (\Saída [8]), .Vem1(ulacell_17_vai1), .B(B8), .A(A[8]),
    .OperCode(OperCode));
  ULAcell ulacell_16 (
    .Vai1(ulacell_16_vai1), .\Saída (\Saída [23]), .Vem1(ulacell_14_vai1), .B(B23), .A(A[23]),
    .OperCode(OperCode));
  ULAcell ulacell_17 (
    .Vai1(ulacell_17_vai1), .\Saída (\Saída [7]), .Vem1(ulacell_19_vai1), .B(B7), .A(A[7]),
    .OperCode(OperCode));
  ULAcell ulacell_18 (
    .Vai1(ulacell_18_vai1), .\Saída (\Saída [24]), .Vem1(ulacell_16_vai1), .B(B24), .A(A[24]),
    .OperCode(OperCode));
  ULAcell ulacell_19 (
    .Vai1(ulacell_19_vai1), .\Saída (\Saída [6]), .Vem1(ulacell_21_vai1), .B(B6), .A(A[6]),
    .OperCode(OperCode));
  ULAcell ulacell_20 (
    .Vai1(ulacell_20_vai1), .\Saída (\Saída [25]), .Vem1(ulacell_18_vai1), .B(B25), .A(A[25]),
    .OperCode(OperCode));
  ULAcell ulacell_21 (
    .Vai1(ulacell_21_vai1), .\Saída (\Saída [5]), .Vem1(ulacell_23_vai1), .B(B5), .A(A[5]),
    .OperCode(OperCode));
  ULAcell ulacell_22 (
    .Vai1(ulacell_22_vai1), .\Saída (\Saída [26]), .Vem1(ulacell_20_vai1), .B(B26), .A(A[26]),
    .OperCode(OperCode));
  ULAcell ulacell_23 (
    .Vai1(ulacell_23_vai1), .\Saída (\Saída [4]), .Vem1(ulacell_25_vai1), .B(B4), .A(A[4]),
    .OperCode(OperCode));
  ULAcell ulacell_24 (
    .Vai1(ulacell_24_vai1), .\Saída (\Saída [27]), .Vem1(ulacell_22_vai1), .B(B27), .A(A[27]),
    .OperCode(OperCode));
  ULAcell ulacell_25 (
    .Vai1(ulacell_25_vai1), .\Saída (\Saída [3]), .Vem1(ulacell_27_vai1), .B(B3), .A(A[3]),
    .OperCode(OperCode));
  ULAcell ulacell_26 (
    .Vai1(ulacell_26_vai1), .\Saída (\Saída [28]), .Vem1(ulacell_24_vai1), .B(B28), .A(A[28]),
    .OperCode(OperCode));
  ULAcell ulacell_27 (
    .Vai1(ulacell_27_vai1), .\Saída (\Saída [2]), .Vem1(ulacell_29_vai1), .B(B2), .A(A[2]),
    .OperCode(OperCode));
  ULAcell ulacell_28 (
    .Vai1(ulacell_28_vai1), .\Saída (\Saída [29]), .Vem1(ulacell_26_vai1), .B(B29), .A(A[29]),
    .OperCode(OperCode));
  ULAcell ulacell_29 (
    .Vai1(ulacell_29_vai1), .\Saída (\Saída [1]), .Vem1(ulacell_31_vai1), .B(B1), .A(A[1]),
    .OperCode(OperCode));
  ULAcell ulacell_30 (
    .Vai1(ulacell_30_vai1), .\Saída (\Saída [30]), .Vem1(ulacell_28_vai1), .B(B30), .A(A[30]),
    .OperCode(OperCode));
  ULAcell ulacell_31 (.Vai1(ulacell_31_vai1), .\Saída (\Saída [0]), .Vem1(1'b0), .B(B0), .A(A[0]), .OperCode(OperCode));
  ULAcell ulacell_32 (
    .Vai1(out_5), .\Saída (\Saída [31]), .Vem1(ulacell_30_vai1), .B(B31), .A(A[31]), .OperCode(OperCode));

  // Other names for the same wires on the sheet: S0 = \Saída [0]; S1 = \Saída [1]; S2 = \Saída [2]; S3 = \Saída [3];
  //   S4 = \Saída [4]; S5 = \Saída [5]; S6 = \Saída [6]; S7 = \Saída [7]; S8 = \Saída [8]; S9 = \Saída [9];
  //   S10 = \Saída [10]; S11 = \Saída [11]; S12 = \Saída [12]; S13 = \Saída [13]; S14 = \Saída [14];
  //   S15 = \Saída [15]; S16 = \Saída [16]; S17 = \Saída [17]; S18 = \Saída [18]; S19 = \Saída [19];
  //   S20 = \Saída [20]; S21 = \Saída [21]; S22 = \Saída [22]; S23 = \Saída [23]; S24 = \Saída [24];
  //   S25 = \Saída [25]; S26 = \Saída [26]; S27 = \Saída [27]; S28 = \Saída [28]; S29 = \Saída [29];
  //   S30 = \Saída [30]; S31 = \Saída [31]
endmodule

module registrador32bits (
  input  [31:0] Entrada,
  input  in_2,
  output [31:0] \Saída 
);

  wire _14;

  D_Flip_Flop d_ff_1 (.clk(in_2), .D(Entrada[0]), .Q(\Saída [0]));  // open: Qn, preset, en, reset
  D_Flip_Flop d_ff_2 (.clk(in_2), .D(Entrada[8]), .Q(\Saída [8]));  // open: Qn, preset, en, reset
  D_Flip_Flop d_ff_3 (.clk(in_2), .D(Entrada[16]), .Q(\Saída [16]));  // open: Qn, preset, en, reset
  D_Flip_Flop d_ff_4 (.clk(in_2), .D(Entrada[24]), .Q(\Saída [24]));  // open: Qn, preset, en, reset
  D_Flip_Flop d_ff_5 (.clk(in_2), .D(Entrada[1]), .Q(\Saída [1]));  // open: Qn, preset, en, reset
  D_Flip_Flop d_ff_6 (.clk(in_2), .D(Entrada[9]), .Q(\Saída [9]));  // open: Qn, preset, en, reset
  D_Flip_Flop d_ff_7 (.clk(in_2), .D(Entrada[17]), .Q(\Saída [17]));  // open: Qn, preset, en, reset
  D_Flip_Flop d_ff_8 (.clk(in_2), .D(Entrada[25]), .Q(\Saída [25]));  // open: Qn, preset, en, reset
  D_Flip_Flop d_ff_9 (.clk(in_2), .D(Entrada[2]), .Q(\Saída [2]));  // open: Qn, preset, en, reset
  D_Flip_Flop d_ff_10 (.clk(in_2), .D(Entrada[10]), .Q(\Saída [10]));  // open: Qn, preset, en, reset
  D_Flip_Flop d_ff_11 (.clk(in_2), .D(Entrada[18]), .Q(\Saída [18]));  // open: Qn, preset, en, reset
  D_Flip_Flop d_ff_12 (.clk(in_2), .D(Entrada[26]), .Q(\Saída [26]));  // open: Qn, preset, en, reset
  D_Flip_Flop d_ff_13 (.clk(in_2), .D(Entrada[3]), .Q(\Saída [3]));  // open: Qn, preset, en, reset
  D_Flip_Flop d_ff_14 (.clk(in_2), .D(Entrada[11]), .Q(\Saída [11]));  // open: Qn, preset, en, reset
  D_Flip_Flop d_ff_15 (.clk(in_2), .D(Entrada[19]), .Q(\Saída [19]));  // open: Qn, preset, en, reset
  D_Flip_Flop d_ff_16 (.clk(in_2), .D(Entrada[27]), .Q(\Saída [27]));  // open: Qn, preset, en, reset
  D_Flip_Flop d_ff_17 (.clk(in_2), .D(Entrada[4]), .Q(\Saída [4]));  // open: Qn, preset, en, reset
  D_Flip_Flop d_ff_18 (.clk(in_2), .D(Entrada[12]), .Q(\Saída [12]));  // open: Qn, preset, en, reset
  D_Flip_Flop d_ff_19 (.clk(in_2), .D(Entrada[20]), .Q(\Saída [20]));  // open: Qn, preset, en, reset
  D_Flip_Flop d_ff_20 (.clk(in_2), .D(Entrada[28]), .Q(\Saída [28]));  // open: Qn, preset, en, reset
  D_Flip_Flop d_ff_21 (.clk(in_2), .D(Entrada[5]), .Q(\Saída [5]));  // open: Qn, preset, en, reset
  D_Flip_Flop d_ff_22 (.clk(in_2), .D(Entrada[13]), .Q(\Saída [13]));  // open: Qn, preset, en, reset
  D_Flip_Flop d_ff_23 (.clk(in_2), .D(Entrada[21]), .Q(\Saída [21]));  // open: Qn, preset, en, reset
  D_Flip_Flop d_ff_24 (.clk(in_2), .D(Entrada[29]), .Q(\Saída [29]));  // open: Qn, preset, en, reset
  D_Flip_Flop d_ff_25 (.clk(in_2), .D(Entrada[6]), .Q(\Saída [6]));  // open: Qn, preset, en, reset
  D_Flip_Flop d_ff_26 (.clk(in_2), .D(_14), .Q(\Saída [14]));  // open: Qn, preset, en, reset
  D_Flip_Flop d_ff_27 (.clk(in_2), .D(Entrada[22]), .Q(\Saída [22]));  // open: Qn, preset, en, reset
  D_Flip_Flop d_ff_28 (.clk(in_2), .D(Entrada[30]), .Q(\Saída [30]));  // open: Qn, preset, en, reset
  D_Flip_Flop d_ff_29 (.clk(in_2), .D(Entrada[7]), .Q(\Saída [7]));  // open: Qn, preset, en, reset
  D_Flip_Flop d_ff_30 (.D(Entrada[15]), .Q(\Saída [15]));  // open: clk, Qn, preset, en, reset
  D_Flip_Flop d_ff_31 (.clk(in_2), .D(Entrada[23]), .Q(\Saída [23]));  // open: Qn, preset, en, reset
  D_Flip_Flop d_ff_32 (.clk(in_2), .D(Entrada[31]), .Q(\Saída [31]));  // open: Qn, preset, en, reset

  // Other names for the same wires on the sheet: E0 = Entrada[0]; E1 = Entrada[1]; E2 = Entrada[2]; E3 = Entrada[3];
  //   E4 = Entrada[4]; E5 = Entrada[5]; E6 = Entrada[6]; E7 = Entrada[7]; E8 = Entrada[8]; E9 = Entrada[9];
  //   E10 = Entrada[10]; E11 = Entrada[11]; E12 = Entrada[12]; E13 = Entrada[13]; E14 = Entrada[14];
  //   E15 = Entrada[15]; E16 = Entrada[16]; E17 = Entrada[17]; E18 = Entrada[18]; E19 = Entrada[19];
  //   E20 = Entrada[20]; E21 = Entrada[21]; E22 = Entrada[22]; E23 = Entrada[23]; E24 = Entrada[24];
  //   E25 = Entrada[25]; E26 = Entrada[26]; E27 = Entrada[27]; E28 = Entrada[28]; E29 = Entrada[29];
  //   E30 = Entrada[30]; E31 = Entrada[31]; S0 = \Saída [0]; S1 = \Saída [1]; S2 = \Saída [2]; S3 = \Saída [3];
  //   S4 = \Saída [4]; S5 = \Saída [5]; S6 = \Saída [6]; S7 = \Saída [7]; S8 = \Saída [8]; S9 = \Saída [9];
  //   S10 = \Saída [10]; S11 = \Saída [11]; S12 = \Saída [12]; S13 = \Saída [13]; S14 = \Saída [14];
  //   S15 = \Saída [15]; S16 = \Saída [16]; S17 = \Saída [17]; S18 = \Saída [18]; S19 = \Saída [19];
  //   S20 = \Saída [20]; S21 = \Saída [21]; S22 = \Saída [22]; S23 = \Saída [23]; S24 = \Saída [24];
  //   S25 = \Saída [25]; S26 = \Saída [26]; S27 = \Saída [27]; S28 = \Saída [28]; S29 = \Saída [29];
  //   S30 = \Saída [30]; S31 = \Saída [31]
endmodule
