// Logisim project ULA32Bits.circ as structural Verilog
module mux16 (
  input  in_1,
  input  in_2,
  input  in_3,
  input  in_4,
  input  in_5,
  input  in_6,
  input  in_7,
  input  in_8,
  input  in_9,
  input  in_10,
  input  in_11,
  input  in_12,
  input  in_13,
  input  in_14,
  input  in_15,
  input  in_16,
  input  [3:0] Sel,
  output out_18
);

  wire and_1_out, and_2_out, and_3_out, and_4_out, and_5_out, and_6_out, and_7_out, and_8_out, and_9_out,
       and_10_out, and_11_out, and_12_out, and_13_out, and_14_out, and_15_out, and_16_out;

  and and_1 (and_1_out, in_1, ~Sel[3], ~Sel[2], ~Sel[1], ~Sel[0]);  // AND_Gate
  and and_2 (and_2_out, in_2, ~Sel[3], ~Sel[2], ~Sel[1], Sel[0]);  // AND_Gate
  and and_3 (and_3_out, in_3, ~Sel[3], ~Sel[2], Sel[1], ~Sel[0]);  // AND_Gate
  and and_4 (and_4_out, in_4, ~Sel[3], ~Sel[2], Sel[1], Sel[0]);  // AND_Gate
  and and_5 (and_5_out, in_5, ~Sel[3], Sel[2], ~Sel[1], ~Sel[0]);  // AND_Gate
  and and_6 (and_6_out, in_6, ~Sel[3], Sel[2], ~Sel[1], Sel[0]);  // AND_Gate
  and and_7 (and_7_out, in_7, ~Sel[3], Sel[2], Sel[1], ~Sel[0]);  // AND_Gate
  and and_8 (and_8_out, in_8, ~Sel[3], Sel[2], Sel[1], Sel[0]);  // AND_Gate
  and and_9 (and_9_out, in_9, Sel[3], ~Sel[2], ~Sel[1], ~Sel[0]);  // AND_Gate
  and and_10 (and_10_out, in_10, Sel[3], ~Sel[2], ~Sel[1], Sel[0]);  // AND_Gate
  and and_11 (and_11_out, in_11, Sel[3], ~Sel[2], Sel[1], ~Sel[0]);  // AND_Gate
  and and_12 (and_12_out, in_12, Sel[3], ~Sel[2], Sel[1], Sel[0]);  // AND_Gate
  and and_13 (and_13_out, in_13, Sel[3], Sel[2], ~Sel[1], ~Sel[0]);  // AND_Gate
  and and_14 (and_14_out, in_14, Sel[3], Sel[2], ~Sel[1], Sel[0]);  // AND_Gate
  and and_15 (and_15_out, in_15, Sel[3], Sel[2], Sel[1], ~Sel[0]);  // AND_Gate
  and and_16 (and_16_out, in_16, Sel[3], Sel[2], Sel[1], Sel[0]);
  or or_1 (out_18, and_1_out, and_2_out, and_3_out, and_4_out, and_5_out, and_6_out, and_7_out, and_8_out, and_9_out, and_10_out, and_11_out, and_12_out, and_13_out, and_14_out, and_15_out, and_16_out);
endmodule

module ULACell (
  input  B,
  input  A,
  input  [3:0] SelectorOperador,
  input  vem_1,
  input  in_5,
  output \Saída ,
  output Vai_1,
  output out_8
);

  wire and_1_out, or_1_out, somc_1_soma, sub_1_soma, xor_1_out;

  and and_1 (and_1_out, A, B);
  or or_1 (or_1_out, A, B);
  xor xor_1 (xor_1_out, A, B);
  SomC somc_1 (.Vai1(Vai_1), .B(B), .A(A), .Soma(somc_1_soma), .V1(vem_1));
  Sub sub_1 (.Vai1(out_8), .B(B), .A(A), .Soma(sub_1_soma), .V1(in_5));
  mux16 mux16_1 (
    .in_1(and_1_out), .in_2(or_1_out), .in_3(xor_1_out), .in_4(somc_1_soma), .in_5(sub_1_soma),
    .Sel(SelectorOperador), .out_18(\Saída ));  // open: in_6, in_7, in_8, in_9, in_10, in_11, in_12, in_13, in_14, in_15, in_16
endmodule

module SomC (
  input  B,
  input  A,
  input  V1,
  output Vai1,
  output Soma
);

  wire and_1_out, and_2_out, and_3_out, xor_1_out;

  or or_1 (Vai1, and_1_out, and_2_out, and_3_out);
  and and_1 (and_1_out, V1, B);
  and and_2 (and_2_out, B, A);
  and and_3 (and_3_out, A, V1);
  xor xor_1 (xor_1_out, A, B);
  xor xor_2 (Soma, xor_1_out, V1);
endmodule

module ULA (
  input  [31:0] A,
  input  [31:0] B,
  input  [3:0] in_3,
  output out_4,
  output [31:0] out_5
);

  wire ulacell_2_vai_1, ulacell_3_p1, ulacell_4_vai_1, ulacell_5_vai_1, ulacell_6_vai_1, ulacell_7_vai_1,
       ulacell_8_vai_1, ulacell_9_vai_1, ulacell_10_vai_1, ulacell_11_vai_1, ulacell_12_vai_1,
       ulacell_13_vai_1, ulacell_14_vai_1, ulacell_15_vai_1, ulacell_16_vai_1, ulacell_17_vai_1,
       ulacell_18_vai_1, ulacell_19_vai_1, ulacell_20_vai_1, ulacell_21_vai_1, ulacell_22_vai_1,
       ulacell_23_vai_1, ulacell_24_p1, ulacell_24_p6, ulacell_26_vai_1, ulacell_27_vai_1, ulacell_28_p1,
       ulacell_28_p6, ulacell_30_vai_1, ulacell_31_vai_1, ulacell_32_vai_1;

  ULACell ulacell_1 (
    .Vai_1(out_4), .B(B[31]), .A(A[31]), .SelectorOperador(in_3), .\Saída (out_5[31]), .vem_1(ulacell_3_p1));  // open: out_8, in_5
  ULACell ulacell_2 (
    .Vai_1(ulacell_2_vai_1), .B(B[29]), .A(A[29]), .SelectorOperador(in_3), .\Saída (out_5[29]),
    .vem_1(ulacell_4_vai_1));  // open: out_8, in_5
  // ULACell ulacell_3: pin names not known; wires that end beside it: ulacell_3_p1, B[30], in_3, A[30], out_5[30], ulacell_2_vai_1
  ULACell ulacell_4 (
    .Vai_1(ulacell_4_vai_1), .B(B[28]), .A(A[28]), .SelectorOperador(in_3), .\Saída (out_5[28]),
    .vem_1(ulacell_5_vai_1));  // open: out_8, in_5
  ULACell ulacell_5 (
    .Vai_1(ulacell_5_vai_1), .B(B[27]), .A(A[27]), .SelectorOperador(in_3), .\Saída (out_5[27]),
    .vem_1(ulacell_6_vai_1));  // open: out_8, in_5
  ULACell ulacell_6 (
    .Vai_1(ulacell_6_vai_1), .B(B[26]), .A(A[26]), .SelectorOperador(in_3), .\Saída (out_5[26]),
    .vem_1(ulacell_7_vai_1));  // open: out_8, in_5
  ULACell ulacell_7 (
    .Vai_1(ulacell_7_vai_1), .B(B[25]), .A(A[25]), .SelectorOperador(in_3), .\Saída (out_5[25]),
    .vem_1(ulacell_8_vai_1));  // open: out_8, in_5
  ULACell ulacell_8 (
    .Vai_1(ulacell_8_vai_1), .B(B[24]), .A(A[24]), .SelectorOperador(in_3), .\Saída (out_5[24]),
    .vem_1(ulacell_9_vai_1));  // open: out_8, in_5
  ULACell ulacell_9 (
    .Vai_1(ulacell_9_vai_1), .B(B[23]), .A(A[23]), .SelectorOperador(in_3), .\Saída (out_5[23]),
    .vem_1(ulacell_10_vai_1));  // open: out_8, in_5
  ULACell ulacell_10 (
    .Vai_1(ulacell_10_vai_1), .B(B[22]), .A(A[22]), .SelectorOperador(in_3), .\Saída (out_5[22]),
    .vem_1(ulacell_11_vai_1));  // open: out_8, in_5
  ULACell ulacell_11 (
    .Vai_1(ulacell_11_vai_1), .B(B[21]), .A(A[21]), .SelectorOperador(in_3), .\Saída (out_5[21]),
    .vem_1(ulacell_12_vai_1));  // open: out_8, in_5
  ULACell ulacell_12 (
    .Vai_1(ulacell_12_vai_1), .B(B[20]), .A(A[20]), .SelectorOperador(in_3), .\Saída (out_5[20]),
    .vem_1(ulacell_13_vai_1));  // open: out_8, in_5
  ULACell ulacell_13 (
    .Vai_1(ulacell_13_vai_1), .B(B[19]), .A(A[19]), .SelectorOperador(in_3), .\Saída (out_5[19]),
    .vem_1(ulacell_15_vai_1));  // open: out_8, in_5
  ULACell ulacell_14 (
    .Vai_1(ulacell_14_vai_1), .B(B[17]), .A(A[17]), .SelectorOperador(in_3), .\Saída (out_5[17]),
    .vem_1(ulacell_16_vai_1));  // open: out_8, in_5
  ULACell ulacell_15 (
    .Vai_1(ulacell_15_vai_1), .B(B[18]), .A(A[18]), .SelectorOperador(in_3), .\Saída (out_5[18]),
    .vem_1(ulacell_14_vai_1));  // open: out_8, in_5
  ULACell ulacell_16 (
    .Vai_1(ulacell_16_vai_1), .B(B[16]), .A(A[16]), .SelectorOperador(in_3), .\Saída (out_5[16]),
    .vem_1(ulacell_17_vai_1));  // open: out_8, in_5
  ULACell ulacell_17 (
    .Vai_1(ulacell_17_vai_1), .B(B[15]), .A(A[15]), .SelectorOperador(in_3), .\Saída (out_5[15]),
    .vem_1(ulacell_18_vai_1));  // open: out_8, in_5
  ULACell ulacell_18 (
    .Vai_1(ulacell_18_vai_1), .B(B[14]), .A(A[14]), .SelectorOperador(in_3), .\Saída (out_5[14]),
    .vem_1(ulacell_19_vai_1));  // open: out_8, in_5
  ULACell ulacell_19 (
    .Vai_1(ulacell_19_vai_1), .B(B[13]), .A(A[13]), .SelectorOperador(in_3), .\Saída (out_5[13]),
    .vem_1(ulacell_20_vai_1));  // open: out_8, in_5
  ULACell ulacell_20 (
    .Vai_1(ulacell_20_vai_1), .B(B[12]), .A(A[12]), .SelectorOperador(in_3), .\Saída (out_5[12]),
    .vem_1(ulacell_21_vai_1));  // open: out_8, in_5
  ULACell ulacell_21 (
    .Vai_1(ulacell_21_vai_1), .B(B[11]), .A(A[11]), .SelectorOperador(in_3), .\Saída (out_5[11]),
    .vem_1(ulacell_23_vai_1));  // open: out_8, in_5
  ULACell ulacell_22 (
    .Vai_1(ulacell_22_vai_1), .B(B[9]), .A(A[9]), .SelectorOperador(in_3), .\Saída (out_5[9]),
    .vem_1(ulacell_24_p1));  // open: out_8, in_5
  ULACell ulacell_23 (
    .Vai_1(ulacell_23_vai_1), .B(B[10]), .A(A[10]), .SelectorOperador(in_3), .\Saída (out_5[10]),
    .vem_1(ulacell_22_vai_1));  // open: out_8, in_5
  // ULACell ulacell_24: pin names not known; wires that end beside it: ulacell_24_p1, B[8], in_3, A[8], out_5[8], ulacell_24_p6
  ULACell ulacell_25 (
    .Vai_1(ulacell_24_p6), .B(B[7]), .A(A[7]), .SelectorOperador(in_3), .\Saída (out_5[7]),
    .vem_1(ulacell_26_vai_1));  // open: out_8, in_5
  ULACell ulacell_26 (
    .Vai_1(ulacell_26_vai_1), .B(B[6]), .A(A[6]), .SelectorOperador(in_3), .\Saída (out_5[6]),
    .vem_1(ulacell_27_vai_1));  // open: out_8, in_5
  ULACell ulacell_27 (
    .Vai_1(ulacell_27_vai_1), .B(B[5]), .A(A[5]), .SelectorOperador(in_3), .\Saída (out_5[5]),
    .vem_1(ulacell_28_p1));  // open: out_8, in_5
  // ULACell ulacell_28: pin names not known; wires that end beside it: ulacell_28_p1, B[4], in_3, A[4], out_5[4], ulacell_28_p6
  ULACell ulacell_29 (
    .Vai_1(ulacell_28_p6), .B(B[3]), .A(A[3]), .SelectorOperador(in_3), .\Saída (out_5[3]),
    .vem_1(ulacell_31_vai_1));  // open: out_8, in_5
  ULACell ulacell_30 (
    .Vai_1(ulacell_30_vai_1), .B(B[1]), .A(A[1]), .SelectorOperador(in_3), .\Saída (out_5[1]),
    .vem_1(ulacell_32_vai_1));  // open: out_8, in_5
  ULACell ulacell_31 (
    .Vai_1(ulacell_31_vai_1), .B(B[2]), .A(A[2]), .SelectorOperador(in_3), .\Saída (out_5[2]),
    .vem_1(ulacell_30_vai_1));  // open: out_8, in_5
  ULACell ulacell_32 (
    .Vai_1(ulacell_32_vai_1), .B(B[0]), .A(A[0]), .SelectorOperador(in_3), .\Saída (out_5[0]), .vem_1(1'b0));  // open: out_8, in_5
endmodule

module Sub (
  input  B,
  input  A,
  input  V1,
  output Vai1,
  output Soma
);

  wire and_1_out, and_2_out, and_3_out, xor_1_out;

  or or_1 (Vai1, and_1_out, and_2_out, and_3_out);
  and and_1 (and_1_out, V1, B);
  and and_2 (and_2_out, B, ~A);  // AND_Gate
  and and_3 (and_3_out, ~A, V1);  // AND_Gate
  xor xor_1 (xor_1_out, A, B);
  xor xor_2 (Soma, xor_1_out, V1);
endmodule
